# Fritzing sketch leaf-energy-meter (saved by Fritzing 1.0.2b)

parts:
  Part1 = Arduino Pro Mini v13
  U1 = OBDII [package=obdii]
  M1 = Niren can bus module [package=THT]
  OLED1 = OLED 128x64 I2C Monochrome Display GND-VDD
  A2 = buck regulator mp1584en

nets:
  N1: Part1.A4, OLED1.SDA
  N2: Part1.A5, OLED1.SCK
  N3: Part1.D13/SCK, M1.pin6
  N4: Part1.D12/MISO, M1.pin4
  N5: Part1.D11_PWM/MOSI, M1.pin5
  N6: Part1.D10_PWM/SS, M1.pin3
  N7: Part1.D2, M1.pin7
  N8: U1.1, A2.Pin_3
  N9: U1.SIGGND, A2.Pin_1, A2.Pin_2
  N10: U1.12, M1.pin10, M1.pin12
  N11: U1.13, M1.pin11, M1.pin13
  N12: OLED1.GND, A2.Pin_7, A2.Pin_8
  N13: OLED1.VDD, A2.Pin_6

custom parts:
  Niren can bus module: Niren can bus module availabe on ebay and others. Pcb view assumes that you unsolder the 7 pin header and resolder it on the bottom of the module to connect to the pcb. The two jumpers and the can bus connector remain on the top of the board and don't appear in pcb view.
  OLED 128x64 I2C Monochrome Display GND-VDD: OLED 128x64 I2C Monochrome Display. Note: there are two variants of this part, this one is the GND VDD SCK SDA variant. The other is VDD GND SCK SDA. Make sure you select the part that matches your module as using the incorrect part will probably destroy your module! In addition the mounting holes are marked on silkscreen but not by default drilled. If you want drilled mounting holes, copy a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
  buck regulator mp1584en: Mini MP1584EN DC to DC buck converter module with a wide operating range.
